# Fritzing sketch flameSensor (saved by Fritzing 0.9.3b)

parts:
  Part1 = Arduino Uno (Rev3) - ICSP
  S1 = KY-026
  J1 = Piezo Speaker

nets:
  N1: Part1.A0, S1.pin1
  N2: Part1.D2, S1.pin4
  N3: Part1.D3_PWM, J1.pin2
  N4: Part1.5V, S1.pin3
  N5: Part1.GND, S1.pin2, J1.pin1

custom parts:
  KY-026: ky-026 flame sensor module
