# Fritzing sketch DS18B20_Arduino (saved by Fritzing 0.9.3b)
breadboards: 1

parts:
  R1 = Resistor [tolerance=±5% resistance=4.7k package="2512 [SMD]"]
  DS1 = DS18B20 1-Wire Temperature Sensor [part_number=DS18B20]
  Part1 = Arduino Uno (Rev3)

nets:
  VDD: R1.Pin_0, DS1.VDD, Part1.5V
  N1: R1.Pin_1, DS1.DQ, Part1.D3_PWM
  GND: DS1.GND, Part1.GND
