# Fritzing sketch LCD16x02Menu (saved by Fritzing 0.9.3b)

parts:
  ENCODER1 = Rotary Encoder
  Part1 = Arduino Uno (Rev3)
  Part2 = LCD1602-I2C

nets:
  VCC: ENCODER1.VCC, Part1.5V, Part2.VCC
  GND: ENCODER1.GND, Part1.GND, Part2.GND
  N1: ENCODER1.SW, Part1.D4
  N2: ENCODER1.GT, Part1.D3_PWM
  N3: ENCODER1.CLK, Part1.D2
  N4: Part1.A4/SDA, Part2.SDA
  N5: Part1.A5/SCL, Part2.SCL

custom parts:
  LCD1602-I2C: A standard character display, usually with 2x16 characters. Comes in many colors with LCM1602 IIC attached.
