# Fritzing sketch Arduino_encoderRotary (saved by Fritzing 0.9.3b)

parts:
  ENCODER1 = Rotary Encoder
  Part1 = Arduino Uno (Rev3)

nets:
  VCC: ENCODER1.VCC, Part1.5V
  GND: ENCODER1.GND, Part1.GND
  N1: ENCODER1.SW, Part1.D4
  N2: ENCODER1.GT, Part1.D3_PWM
  N3: ENCODER1.CLK, Part1.D2
