# Fritzing sketch neoPixel (saved by Fritzing 0.9.3b)
breadboards: 3

parts:
  Part6 = Arduino Uno (Rev3) - ICSP
  S4 = Round Pushbutton
  U3 = WS2812 RGB LED matrix 1x8
  Part7 = 12 NeoPixel Ring [part_number=1643]
  R1 = Resistor [tolerance=±5% resistance=220 package="0805 [SMD]"]
  Part5 = 12 NeoPixel Ring [part_number=1643]
  Part8 = 12 NeoPixel Ring [part_number=1643]  # not connected
  R3 = Resistor [tolerance=±5% resistance=220 package=THT]
  Part1 = Arduino Uno (Rev3) - ICSP
  Part4 = Arduino Uno (Rev3) - ICSP
  U2 = WS2812 RGB LED matrix 1x8
  Part3 = 12 NeoPixel Ring [part_number=1643]
  R2 = Resistor [tolerance=±5% resistance=220 package=THT]
  U4 = WS2812 RGB LED matrix 1x8  # not connected

nets:
  N1: Part6.D2, S4.leg0
  N2: Part6.D6_PWM, R1.Pin_1
  5V: Part6.5V, U3.VCC, Part7.VDD
  GND: Part6.GND, S4.leg1, U3.GND, Part7.GND
  N3: U3.DIN, Part7.OUT
  N4: Part7.IN, R1.Pin_0
  N5: Part5.IN, R2.Pin_0
  N6: Part5.OUT, U2.DIN
  VDD: Part5.VDD, Part4.5V, U2.VCC
  GND_2: Part5.GND, Part4.GND, U2.GND
  N7: R3.Pin_0, Part3.IN
  N8: R3.Pin_1, Part1.D6_PWM
  5V_2: Part1.5V, Part3.VDD
  GND_3: Part1.GND, Part3.GND

custom parts:
  WS2812 RGB LED matrix 1x8: WS2812 matrix 1x8
  12 NeoPixel Ring: 12 ultra bright smart LED NeoPixels are arranged in a circle with 1.5" (37mm) outer diameter. The rings are 'chainable' - connect the output pin of one to the input pin of another. Use only one microcontroller pin to control as many as you can chain together! Each LED is addressable as the driver chip is inside the LED. Each one has ~18mA constant current drive so the color will be very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
