# Fritzing sketch sim800l (saved by Fritzing 0.9.3b)

parts:
  Part2 = Arduino Uno (Rev3)
  R6 = Resistor [tolerance=±5% resistance=20k package="0402 [SMD]"]
  R7 = Resistor [tolerance=±5% resistance=10k package="0402 [SMD]"]
  SIM800L2 = SIM800L
  BATT2 = LiPoly Battery (1300mAh)

nets:
  N1: Part2.GND, R6.Pin_1
  N2: Part2.D2, R7.Pin_1
  N3: Part2.D3_PWM, SIM800L2.TXD
  N4: R7.Pin_0, SIM800L2.RXD
  N5: SIM800L2.VCC, BATT2.positive
  N6: SIM800L2.GND, BATT2.negative

custom parts:
  SIM800L: SIM800L is a miniature cellular module which allows for GPRS transmission, sending and receiving SMS and making and receiving voice calls. Low cost and small footprint and quad band frequency support make this module perfect solution for any project that require long range connectivity. After connecting power module boots up, searches for cellular network and login automatically. On board LED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
  LiPoly Battery (1300mAh): Lithium Ion Polymer Battery (1300mAh)
