# Fritzing sketch NTC_B3950 (saved by Fritzing 0.9.3b)

parts:
  Part2 = Arduino Uno (Rev3)
  R4 = Temperature Sensor (Thermistor) [thermistor_type=NTC package=THT]
  R = Resistor [tolerance=±5% resistance=10k package="0402 [SMD]"]

nets:
  N1: Part2.A0, R4.pin_0, R.Pin_0
  N2: Part2.GND, R.Pin_1
  N3: Part2.5V, R4.pin_1
