# Fritzing sketch Auto-Santinizer (saved by Fritzing 0.9.3b)

parts:
  Part1 = Arduino Uno (Rev3)
  hc-sr1 = hc-sr04
  J1 = Basic Servo

nets:
  N1: Part1.D10_PWM/SS, J1.pulse
  N2: Part1.D11_PWM/MOSI, hc-sr1.Trig
  N3: Part1.D12/MISO, hc-sr1.Echo
  VCC: Part1.5V, hc-sr1.VCC, J1.vcc
  GND: Part1.GND, hc-sr1.GND, J1.gnd
