# Fritzing sketch Diagram (saved by Fritzing 0.9.3b)
breadboards: 1

parts:
  Part1 = Arduino Uno (Rev3)
  TCS1 = TCS3200
  U1 = 2-Channel 5v Relay Shield [package=relay-2ch5v10a]

nets:
  N1: Part1.D8, TCS1.OUT
  N2: Part1.D11_PWM/MOSI, U1.IN1
  N3: Part1.D12/MISO, U1.IN2
  N4: Part1.D4, TCS1.S0
  N5: Part1.D5_PWM, TCS1.S1
  N6: Part1.D6_PWM, TCS1.S2
  N7: Part1.D7, TCS1.S3
  5V: Part1.5V, U1.VCC
  GND: Part1.GND, U1.GND

custom parts:
  TCS3200: COLOR SENSING TCS3200
  2-Channel 5v Relay Shield: 2 Channel 5v Relay Shield w. 2x SPD-06VDC-SD-C
