# Fritzing sketch Flame_Rain_Light_Uno (saved by Fritzing 0.9.3b)

parts:
  Part1 = Arduino Uno (Rev3)
  YL-83_-_Detection_Board1 = YL-83 Rain Sensor - Detection Board
  YL-83_-_Control_Board1 = YL-83 Rain Sensor - Control Board
  Mod1 = KY-026 Flame Sensor Module [package="Breakout board"]
  e-radionica_com1 = LM393 LDR breakout [part_number=100027]
  LED1 = smd LED [color="Red (633nm)" package="1206 [SMD]"]
  R1 = Resistor [tolerance=±5% resistance=220 package="2010 [SMD]"]
  J1 = Piezo Speaker
  M1 = DC Motor

nets:
  N1: Part1.D8, LED1.anode
  N2: Part1.D9_PWM, J1.pin2
  N3: Part1.D10_PWM/SS, M1.pin_2
  N4: Part1.D5_PWM, Mod1.D0
  N5: Part1.D6_PWM, e-radionica_com1.DO
  N6: Part1.D7, YL-83_-_Control_Board1.DO
  5V: Part1.5V, YL-83_-_Control_Board1.VCC
  GND: Part1.GND, YL-83_-_Control_Board1.GND
  N7: YL-83_-_Detection_Board1.POS, YL-83_-_Control_Board1.POS
  N8: YL-83_-_Detection_Board1.NEG, YL-83_-_Control_Board1.NEG
  N9: LED1.cathode, R1.Pin_0

custom parts:
  YL-83 Rain Sensor - Detection Board: The YL-83 is a rain sensor that has more resistance when dry and less resistance when wet. The module runs at 5V.
  YL-83 Rain Sensor - Control Board: The YL-83 is a rain sensor that has more resistance when dry and less resistance when wet. The module runs at 5V.
  KY-026 Flame Sensor Module: KY-026 Flame Sensor Module reacts in the presence of fire.
