# Fritzing sketch mayHanCell (saved by Fritzing 0.9.3b)

parts:
  ENCODER1 = Rotary Encoder
  Part2 = LCD1602-I2C
  M2 = Stepper Motor - Unipolar
  S1 = Round Pushbutton
  Part3 = Arduino Nano (Rev3.0)
  Mod2 = KY-019 5V Relay Module [package="Breakout board"]

nets:
  GND: ENCODER1.GND, S1.leg0, Part3.GND, Mod2.-
  N1: ENCODER1.SW, Part3.D5
  N2: ENCODER1.GT, Part3.D3
  N3: ENCODER1.CLK, Part3.D2
  N4: Part2.SDA, Part3.A4
  N5: Part2.SCL, Part3.A5
  N6: M2.A, Part3.D13/SCK
  N7: M2.C, Part3.D12/MISO
  N8: M2.COMMON_2, Part3.D11/MOSI
  N9: S1.leg1, Part3.D10
  N10: Part3.D8, Mod2.S
  N11: Part3.5V, Mod2.+

notes:
  EN DIR PUL

custom parts:
  LCD1602-I2C: A standard character display, usually with 2x16 characters. Comes in many colors with LCM1602 IIC attached.
  KY-019 5V Relay Module: KY-019 5V Relay module, used to control AC circuits. (Special thanks to vanepp for fixing the PCB holes and other errors)
