# Fritzing sketch Stepper_TB6560_LCD (saved by Fritzing 0.9.3b)

parts:
  Part1 = Arduino Uno (Rev3)
  Part2 = LCD1602-I2C
  JACK1 = 2.1mm Barrel Jack with Terminal Block  # not connected
  R1 = Resistor [tolerance=±5% resistance=220 package="1206 [SMD]"]
  S2 = SWITCH-MOMENTARY-2 [package=tactile-pth-12mm]
  R2 = Resistor [tolerance=±5% resistance=220 package="1206 [SMD]"]
  S3 = SWITCH-MOMENTARY-2 [package=tactile-pth-12mm]
  R3 = Resistor [tolerance=±5% resistance=220 package="1206 [SMD]"]
  S4 = SWITCH-MOMENTARY-2 [package=tactile-pth-12mm]

nets:
  N1: Part1.A0, R1.Pin_0, S2.2
  N2: Part1.A1, R2.Pin_0, S3.2
  N3: Part1.A2, R3.Pin_0, S4.2
  N4: Part1.A4/SDA, Part2.SDA
  N5: Part1.A5/SCL, Part2.SCL
  5V: Part1.5V, Part2.VCC
  GND: Part1.GND, Part2.GND, R1.Pin_1, R2.Pin_1, R3.Pin_1

custom parts:
  LCD1602-I2C: A standard character display, usually with 2x16 characters. Comes in many colors with LCM1602 IIC attached.
