# Fritzing sketch DataLogging_DS1302_DHT11 fritzing (saved by Fritzing 0.9.3b)

parts:
  Part1 = Arduino Uno (Rev3)
  sdCard1 = my_sdCard
  DHT1 = Humidity and Temperature Sensor DHT11
  MH-Real-Time_Clock_Module_3 = RTC_DS1302_module

nets:
  N1: Part1.D10_PWM/SS, sdCard1.CS
  N2: Part1.D11_PWM/MOSI, sdCard1.MOSI
  N3: Part1.D12/MISO, sdCard1.MISO
  N4: Part1.D13/SCK, sdCard1.SCK
  N5: Part1.D2, DHT1.Data-signal
  N6: Part1.D3_PWM, MH-Real-Time_Clock_Module_3.RST
  N7: Part1.D4, MH-Real-Time_Clock_Module_3.DAT
  N8: Part1.D5_PWM, MH-Real-Time_Clock_Module_3.CLK
  5V: Part1.5V, sdCard1.VCC
  GND: Part1.GND, sdCard1.GND

notes:
  CONNECTIONS:
  DS1302 CLK/SCLK --> 5
  DS1302 DAT/IO --> 4
  DS1302 RST/CE --> 3
  DS1302 VCC --> 3.3v - 5v
  DS1302 GND --> GND
  DHT11 VCC --> 5V
  DHT11 GND --> GND
  DHT11 OUT --> 2
  SD MOSI --> 11
  SD MISO --> 12
  SD CLK --> 13
  SD CS --> 10

custom parts:
  my_sdCard: micro sdCard Adapter with 90º pin header. Use a filtering Capacitor between CS and GND if needed. PCB View Pinouts are Reversed for laying parallel on PCB using a 90º pin header.
  Humidity and Temperature Sensor DHT11: Digital relative humidity & temperature sensor DHT11
  RTC_DS1302_module: Arduino module DS1302 SPI Real Time Clock
