# Fritzing sketch sdCard_HCSR04 (saved by Fritzing 0.9.3b)
breadboards: 1

parts:
  Part1 = Arduino Uno (Rev3)
  sdCard1 = my_sdCard
  hc-sr1 = hc-sr04
  S2 = Round Pushbutton

nets:
  N1: Part1.D10_PWM/SS, sdCard1.CS
  N2: Part1.D11_PWM/MOSI, sdCard1.MOSI
  N3: Part1.D12/MISO, sdCard1.MISO
  N4: Part1.D13/SCK, sdCard1.SCK
  N5: Part1.D2, hc-sr1.Echo
  N6: Part1.D3_PWM, hc-sr1.Trig
  N7: Part1.D4, S2.leg0
  5V: Part1.5V, sdCard1.VCC
  GND: Part1.GND, sdCard1.GND

notes:
  SD UNO
  GND GND
  5V 5V
  MISO pin 12
  MOSI pin 11
  CLK pin 13
  CS pin 10

custom parts:
  my_sdCard: micro sdCard Adapter with 90º pin header. Use a filtering Capacitor between CS and GND if needed. PCB View Pinouts are Reversed for laying parallel on PCB using a 90º pin header.
