# Fritzing sketch Direction_sw_3status (saved by Fritzing 0.9.3b)

parts:
  Part1 = Arduino Uno (Rev3) - ICSP
  M1 = Stepper Motor - Unipolar
  S14 = Toggle Switch spdt [package=THT]
  R3 = Resistor [tolerance=±5% resistance=220 package=THT]
  R4 = Resistor [tolerance=±5% resistance=220 package=THT]

nets:
  N1: Part1.A0, S14.COM, R3.Pin_0, R4.Pin_1
  N2: Part1.D2, M1.COMMON_2
  N3: Part1.D5_PWM, M1.COMMON_1
  N4: Part1.5V, S14.L2, R3.Pin_1
  N5: Part1.GND, S14.L1, R4.Pin_0

notes:
  A4988
  Dir X Pul X

custom parts:
  Toggle Switch spdt: Toggle Switch single pole double throw
