# Fritzing sketch pico-step-tb6600 (saved by Fritzing 0.9.3b)

parts:
  M4 = Stepper Motor - Unipolar
  Mod1 = Raspberry Pi Pico
  S1 = Toggle Switch spdt [package=THT]
  U1 = LM2596 step down module
  JACK1 = 2.1mm Barrel Jack with Terminal Block

nets:
  N1: M4.COMMON_1, Mod1.pin_26, Mod1.pin_29
  N2: M4.B, Mod1.pin_25
  N3: M4.COMMON_2, Mod1.pin_3, Mod1.pin_23, Mod1.pin_28, Mod1.pin_38, Mod1.pin_42, S1.COM, U1.IN-, U1.OUT-, JACK1.NEG
  N4: M4.D, Mod1.pin_24
  N5: Mod1.pin_27, S1.L2
  N6: Mod1.pin_39, U1.OUT+
  N7: U1.IN+, JACK1.POS

notes:
  Driver TB6600
  EN+ PUL+ DIR+ PUL-DIR-EN-
  20 19 18 GND
  VSYS: 1.8V to 5.5V
  +24V

custom parts:
  Raspberry Pi Pico: Raspberry Pi Pico. Based around the RP2040 microcontroller the Pico is a low cost microcontroller device bringing Raspberry Pi quality, cost, and easy of use to the microcontroller space. Jan 2021, Split part in to two versions: SMD (this one) and tht. This one is single sided and uses the castellation pads to solder the module to the board (no holes, other than for the USB connector!). The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
  Toggle Switch spdt: Toggle Switch single pole double throw
  LM2596 step down module: LM2596 DC-DC step down power supply module 3 A.
