# Fritzing sketch Ramp15_Test_6stepper (saved by Fritzing 0.9.3b)

parts:
  DRV_1 = DRV 8825 Stepper Motor Carrier, High Current [part_number="DRV 8825"]
  X = Stepper Motor - Bipolar
  Part1 = Arduino Mega 2560 (Rev3)
  DRV_2 = DRV 8825 Stepper Motor Carrier, High Current [part_number="DRV 8825"]
  Y = Stepper Motor - Bipolar
  DRV_3 = DRV 8825 Stepper Motor Carrier, High Current [part_number="DRV 8825"]
  Z1 = Stepper Motor - Bipolar
  Z2 = Stepper Motor - Bipolar
  DRV_5 = DRV 8825 Stepper Motor Carrier, High Current [part_number="DRV 8825"]
  E0 = Stepper Motor - Bipolar
  DRV_6 = DRV 8825 Stepper Motor Carrier, High Current [part_number="DRV 8825"]
  E1 = Stepper Motor - Bipolar
  DRV_7 = DRV 8825 Stepper Motor Carrier, High Current [part_number="DRV 8825"]  # not connected

nets:
  N1: DRV_1.ENABLE, Part1.D38
  N2: DRV_1.STEP, Part1.A0
  N3: DRV_1.DIRECTION, Part1.A1
  N4: DRV_1.OUT_2B, X.A
  N5: DRV_1.OUT_2A, X.C
  N6: DRV_1.OUT_1A, X.B
  N7: DRV_1.OUT_1B, X.D
  N8: Part1.A8, DRV_3.ENABLE
  N9: Part1.A2, DRV_2.ENABLE
  N10: Part1.A6, DRV_2.STEP
  N11: Part1.A7, DRV_2.DIRECTION
  N12: Part1.D24, DRV_5.ENABLE
  N13: Part1.D26, DRV_5.STEP
  N14: Part1.D28, DRV_5.DIRECTION
  N15: Part1.D30, DRV_6.ENABLE
  N16: Part1.D34, DRV_6.DIRECTION
  N17: Part1.D36, DRV_6.STEP
  N18: Part1.D46, DRV_3.STEP
  N19: Part1.D48, DRV_3.DIRECTION
  N20: DRV_2.OUT_2B, Y.A
  N21: DRV_2.OUT_2A, Y.C
  N22: DRV_2.OUT_1A, Y.B
  N23: DRV_2.OUT_1B, Y.D
  N24: DRV_3.OUT_2B, Z1.A, Z2.A
  N25: DRV_3.OUT_2A, Z1.C, Z2.C
  N26: DRV_3.OUT_1A, Z1.B, Z2.B
  N27: DRV_3.OUT_1B, Z1.D, Z2.D
  N28: DRV_5.OUT_2B, E0.A
  N29: DRV_5.OUT_2A, E0.C
  N30: DRV_5.OUT_1A, E0.B
  N31: DRV_5.OUT_1B, E0.D
  N32: DRV_6.OUT_2B, E1.A
  N33: DRV_6.OUT_2A, E1.C
  N34: DRV_6.OUT_1A, E1.B
  N35: DRV_6.OUT_1B, E1.D

notes:
  2B
  2A
  1A
  1B
  ENA
  STP
  DIR
