# Fritzing sketch setHomeX (saved by Fritzing 0.9.3b)

parts:
  Part1 = Arduino Uno (Rev3) - ICSP
  M2 = Stepper Motor - Unipolar
  S1 = Limit Switch [package="Breakout Board"]
  S2 = Limit Switch [package="Breakout Board"]

nets:
  N1: Part1.D9_PWM, S1.S
  N2: Part1.D11_PWM/MOSI, S2.S
  N3: Part1.D2, M2.COMMON_2
  N4: Part1.D5_PWM, M2.COMMON_1
  N5: Part1.5V, S1.V, S2.V
  N6: Part1.GND, S1.G, S2.G

notes:
  Driver A4988
  Dir X Pul X

custom parts:
  Limit Switch: Generic limit switch commonly found on 3D printers. Typical lever microswitch mounted on a PCB board with a 3 pin JST XH connector.
