# Fritzing sketch TB6600_LCD (saved by Fritzing 0.9.3b)
breadboards: 1

parts:
  Part1 = Arduino Uno (Rev3) - ICSP
  MODE = Pushbutton [package="[SMD]"]
  DOWN = Pushbutton [package="[SMD]"]
  RUN = Pushbutton [package="[SMD]"]
  UP = Pushbutton [package="[SMD]"]
  Part3 = LCD1602-I2C
  M4 = Stepper Motor - Unipolar

nets:
  N1: Part1.A4/SDA, Part3.SDA
  N2: Part1.A5/SCL, Part3.SCL
  N3: Part1.ICSP_MOSI, Part1.D11_PWM/MOSI, UP.Pin_1, UP.Pin_2
  N4: Part1.D8, M4.D
  N5: Part1.D9_PWM, DOWN.Pin_1, DOWN.Pin_2
  N6: Part1.D10_PWM/SS, MODE.Pin_1, MODE.Pin_2
  N7: Part1.D12/MISO, RUN.Pin_1, RUN.Pin_2
  N8: Part1.D2, M4.COMMON_1
  N9: Part1.D5_PWM, M4.B
  5V: Part1.5V, Part3.VCC
  GND: Part1.GND, MODE.Pin_3, MODE.Pin_4, DOWN.Pin_3, DOWN.Pin_4, RUN.Pin_3, RUN.Pin_4, UP.Pin_3, UP.Pin_4, Part3.GND, M4.COMMON_2

notes:
  Driver TB6600
  PUL+ DIR+ EN+ PUL-DIR-EN-

custom parts:
  LCD1602-I2C: A standard character display, usually with 2x16 characters. Comes in many colors with LCM1602 IIC attached.
