# Fritzing sketch Stepper_TB6650_LCD (saved by Fritzing 0.9.3b)

parts:
  ENCODER1 = Rotary Encoder
  Part1 = Arduino Uno (Rev3)
  Part2 = LCD1602-I2C
  M2 = Stepper Motor - Unipolar
  JACK1 = 2.1mm Barrel Jack with Terminal Block
  TRM1 = Terminal 2pin
  TRM2 = Terminal 2pin
  TRM3 = Terminal 2pin
  TRM4 = Terminal 2pin
  TRM5 = Terminal 2pin
  TRM6 = Terminal 2pin

nets:
  VCC: ENCODER1.VCC, Part1.5V, Part2.VCC
  GND: ENCODER1.GND, Part1.GND, Part2.GND, TRM5.pin_2
  N1: ENCODER1.SW, Part1.D11_PWM/MOSI
  N2: ENCODER1.GT, Part1.D10_PWM/SS
  N3: ENCODER1.CLK, Part1.D9_PWM
  N4: Part1.A4/SDA, Part2.SDA
  N5: Part1.A5/SCL, Part2.SCL
  N6: Part1.D8, TRM5.pin_1
  N7: Part1.D2, TRM6.pin_1
  N8: Part1.D5_PWM, TRM4.pin_1
  N9: M2.A, TRM2.pin_2
  N10: M2.C, TRM2.pin_1
  N11: M2.B, TRM1.pin_2
  N12: M2.D, TRM1.pin_1
  N13: JACK1.POS, TRM3.pin_1
  N14: JACK1.NEG, TRM3.pin_2
  N15: TRM4.pin_2, TRM6.pin_2

custom parts:
  LCD1602-I2C: A standard character display, usually with 2x16 characters. Comes in many colors with LCM1602 IIC attached.
  Terminal 2pin: 2-pin Terminal Block
