# Fritzing sketch Stepper_position_pot (saved by Fritzing 0.9.3b)

parts:
  DRV_1 = DRV 8825 Stepper Motor Carrier, High Current [part_number="DRV 8825"]
  X = Stepper Motor - Bipolar
  DRV_7 = DRV 8825 Stepper Motor Carrier, High Current [part_number="DRV 8825"]  # not connected
  Part2 = Arduino Uno (Rev3)
  U1 = POT [package=pot_mammoth]

nets:
  N1: DRV_1.ENABLE, Part2.D8
  N2: DRV_1.STEP, Part2.D2
  N3: DRV_1.DIRECTION, Part2.D3_PWM
  N4: DRV_1.OUT_2B, X.A
  N5: DRV_1.OUT_2A, X.C
  N6: DRV_1.OUT_1A, X.B
  N7: DRV_1.OUT_1B, X.D
  N8: Part2.A0, U1.A
  N9: Part2.5V, U1.E
  N10: Part2.GND, U1.S

notes:
  2B
  2A
  1A
  1B
  ENA
  STP
  DIR
